// Logisim project 8 bit ALU.circ as structural Verilog: 1 circuit, main circuit main
module main (
  input  [7:0] B,
  input  [7:0] A,
  input  [2:0] S,
  output out_4,
  output out_5,
  output [7:0] out_6,
  output [7:0] \output ,
  output [7:0] out_8
);

  wire [7:0] adder_1_out, and_1_out, divider_1_out, multiplier_1_out, nand_1_out, nor_1_out, or_1_out,
       subtractor_1_out;

  Adder adder_1 (.a(A), .b(B), .out(adder_1_out), .cout(out_4));  // open: cin
  Subtractor subtractor_1 (.a(A), .b(B), .out(subtractor_1_out), .bout(out_5));  // open: bin
  Multiplier multiplier_1 (.a(A), .b(B), .out(multiplier_1_out), .cout(out_6));  // open: cin
  Divider divider_1 (.a(A), .b(B), .out(divider_1_out), .rem(out_8));  // open: upper
  assign and_1_out = A & B;  // AND_Gate and_1, 8 bits wide
  assign or_1_out = A | B;  // OR_Gate or_1, 8 bits wide
  assign nand_1_out = ~(A & B);  // NAND_Gate nand_1, 8 bits wide
  assign nor_1_out = ~(A | B);  // NOR_Gate nor_1, 8 bits wide
  Multiplexer #(.select(3), .width(8), .enable("false")) multiplexer_1 (
    .in0(adder_1_out), .in1(subtractor_1_out), .in2(multiplier_1_out), .in3(divider_1_out), .in4(and_1_out),
    .in5(or_1_out), .in6(nand_1_out), .in7(nor_1_out), .out(\output ), .sel(S));

  // Notes on the sheet:
  //   8-bit ALU Design
endmodule
